// Digital circuit ALU.dig as structural Verilog
module ALU (
  input  [7:0] A,
  input  [7:0] B,
  input  F0,
  input  F1,
  input  F2,
  input  F3,
  output [7:0] out,
  output zero,
  output negative,
  output carry,
  output overflow
);

  wire add_1_c_o, add_2_c_o, add_3_c_o, add_4_c_o, and_2_out, and_3_out, and_4_out, and_5_out, not_2_out,
       not_3_out, not_4_out, not_5_out, not_6_out, not_7_out, not_8_out, not_9_out, not_10_out, not_11_out,
       xnor_1_out, xor_1_out;
  wire [7:0] add_1_s, add_2_s, add_3_s, add_4_s, and_1_out, barrelshifter_1_out, barrelshifter_2_out,
       not_1_out, not_12_out, or_1_out;

  assign not_1_out = ~B;  // Not not_1, 8 bits wide
  Add #(.Bits(8)) add_1 (.a(A), .b(8'h1), .c_i(1'b0), .s(add_1_s), .c_o(add_1_c_o));
  Add #(.Bits(8)) add_2 (.a(B), .b(8'h1), .c_i(1'b0), .s(add_2_s), .c_o(add_2_c_o));
  Add #(.Bits(8)) add_3 (.a(B), .b(A), .c_i(1'b0), .s(add_3_s), .c_o(add_3_c_o));
  Add #(.Bits(8)) add_4 (.a(A), .b(not_1_out), .c_i(1'b1), .s(add_4_s), .c_o(add_4_c_o));
  assign and_1_out = A & B;  // And and_1, 8 bits wide
  assign or_1_out = A | B;  // Or or_1, 8 bits wide
  BarrelShifter #(.Bits(8)) barrelshifter_1 (.in(A), .shift(B[3:0]), .out(barrelshifter_1_out));
  BarrelShifter #(.Bits(8), .direction("right")) barrelshifter_2 (.in(A), .shift(B[3:0]), .out(barrelshifter_2_out));
  xor xor_1 (xor_1_out, A[7], B[7]);
  not not_2 (not_2_out, F2);
  not not_3 (not_3_out, F0);
  not not_4 (not_4_out, F3);
  not not_5 (not_5_out, F1);
  not not_6 (not_6_out, F0);
  not not_7 (not_7_out, F3);
  not not_8 (not_8_out, F2);
  not not_9 (not_9_out, F0);
  not not_10 (not_10_out, F1);
  not not_11 (not_11_out, F0);
  and and_2 (and_2_out, F3, not_2_out, F1, not_3_out, add_4_c_o);
  and and_3 (and_3_out, not_4_out, F2, not_5_out, not_6_out, add_1_c_o);
  and and_4 (and_4_out, not_7_out, not_8_out, F1, not_9_out, add_3_c_o);
  and and_5 (and_5_out, F3, F2, not_10_out, not_11_out, add_2_c_o);
  Multiplexer #(.Selector_Bits(4), .Bits(8)) multiplexer_1 (
    .sel({F0, F1, F2, F3}), .in_0(A), .in_1(B), .in_2(add_1_s), .in_3(add_2_s), .in_4(add_3_s),
    .in_5(add_4_s), .in_6(and_1_out), .in_7(or_1_out), .in_8(barrelshifter_1_out),
    .in_9(barrelshifter_2_out), .in_10({8{1'b0}}), .in_11({8{1'b0}}), .in_12({8{1'b0}}), .in_13({8{1'b0}}),
    .in_14({8{1'b0}}), .in_15({8{1'b0}}), .out({negative, out[6:0]}));
  assign not_12_out = ~{negative, out[6:0]};  // Not not_12, 8 bits wide
  or or_2 (carry, and_2_out, and_3_out, and_4_out, and_5_out);
  xnor xnor_1 (xnor_1_out, negative, A[7]);
  and and_6 (overflow, xnor_1_out, xor_1_out);
  and and_7 (zero, not_12_out[0], not_12_out[1], not_12_out[2], not_12_out[3], not_12_out[4], not_12_out[5], not_12_out[6], not_12_out[7]);

  assign out[7] = negative;
endmodule
