// Digital circuit CPUControlUnit.dig as structural Verilog
module CPUControlUnit (
  input  clock,
  input  en1,
  input  sel1,
  input  [7:0] Input,
  input  en3,
  input  en2,
  input  [5:0] A,
  input  sel2,
  output z,
  output n,
  output c,
  output o,
  output [5:0] e
);

  wire cpudatapath_1_x3, cpudatapath_1_x4, not_1_out;
  wire [1:0] MIR_q_3;
  wire [3:0] cpudatapath_1_x1, cpudatapath_1_x2, MIR_q_2;
  wire [4:0] MIR_q_4;
  wire [5:0] multiplexer_1_out;
  wire [6:0] MIR_q;
  wire [17:0] control_store_d, MBR_q;

  ROM #(.AddrBits(6), .Bits(18)) control_store (.A(A), .sel(sel1), .D(control_store_d));
  not not_1 (not_1_out, clock);
  Register #(.Bits(18)) MIR (.D(control_store_d), .C(not_1_out), .en(en1), .Q({MIR_q_4, MIR_q_3, MIR_q_2, MIR_q}));
  Register #(.Bits(18)) MBR (.D(control_store_d), .C(clock), .en(en2), .Q(MBR_q));
  CPUDataPath cpudatapath_1 (
    .Input(Input), .Out_Wr(MIR_q_4[0]), .PC_Wr(MIR_q_4[1]), .MBR_Wr(MIR_q_4[2]), .B_Wr(MIR_q_4[3]),
    .A_Wr(MIR_q_4[4]), .MUX_Ctrl(MIR_q_3), .ALU_Sel(MIR_q_2), .clock(clock), .ROM_Sel(sel2), .z(z), .n(n),
    .c(c), .o(o), .x1(cpudatapath_1_x1), .x2(cpudatapath_1_x2), .x3(cpudatapath_1_x3), .x4(cpudatapath_1_x4));
  Multiplexer #(.Bits(6)) multiplexer_1 (
    .sel(MIR_q[6]), .in_0(MIR_q[5:0]), .in_1(MBR_q[17:12]), .out(multiplexer_1_out));
  Seven_Seg_Hex seven_seg_hex_1 (.d(cpudatapath_1_x1), .dp(cpudatapath_1_x3));
  Register #(.Bits(6)) MPC (.D(multiplexer_1_out), .C(clock), .en(en3), .Q(e));
  Seven_Seg_Hex seven_seg_hex_2 (.d(cpudatapath_1_x2), .dp(cpudatapath_1_x4));

  // Notes on the sheet:
  //   contents of control_store (hex, n*v repeats v):
  //   1004,21c0,31c8,800,0,60e0,70e1,0,9000,a010,0,c004,d0a0,e0a8,0
  //   ,10004,110a0,120a1,131c0,141c8,0,16100,17101,0,19000,1a002,0,1c200
  //   ,1d201,0,1f004,200a0,210a2,221c0,231c8,0,25400,26401,0,28480,29481
  //   ,0,2a000
endmodule
