// Digital circuit CPUDataPath.dig as structural Verilog
module CPUDataPath (
  input  [7:0] Input,
  input  Out_Wr,
  input  PC_Wr,
  input  MBR_Wr,
  input  B_Wr,
  input  A_Wr,
  input  [1:0] MUX_Ctrl,
  input  [3:0] ALU_Sel,
  input  clock,
  input  ROM_Sel,
  output z,
  output n,
  output c,
  output o,
  output [3:0] x1,
  output [3:0] x2,
  output x3,
  output x4
);

  wire [1:0] PC_q;
  wire [5:0] PC_q_2;
  wire [7:0] A_q, alu_1_out, B_q, MBR_q, multiplexer_1_out, rom_1_d;

  ROM #(.AddrBits(6), .Bits(8)) rom_1 (.A(PC_q_2), .sel(ROM_Sel), .D(rom_1_d));
  Register #(.Bits(8)) OUT (.D(alu_1_out), .C(clock), .en(Out_Wr), .Q({x2, x1}));
  Register #(.Bits(8)) PC (.D(alu_1_out), .C(clock), .en(PC_Wr), .Q({PC_q_2, PC_q}));
  Register #(.Bits(8)) MBR (.D(rom_1_d), .C(clock), .en(MBR_Wr), .Q(MBR_q));
  Register #(.Bits(8)) B (.D(alu_1_out), .C(clock), .en(B_Wr), .Q(B_q));
  Register #(.Bits(8)) A (.D(alu_1_out), .C(clock), .en(A_Wr), .Q(A_q));
  Multiplexer #(.Selector_Bits(2), .Bits(8)) multiplexer_1 (
    .sel(MUX_Ctrl), .in_0(Input), .in_1({PC_q_2, PC_q}), .in_2(MBR_q), .in_3(B_q), .out(multiplexer_1_out));
  ALU alu_1 (
    .A(A_q), .B(multiplexer_1_out), .F0(ALU_Sel[3]), .F1(ALU_Sel[2]), .F2(ALU_Sel[1]), .F3(ALU_Sel[0]),
    .out(alu_1_out), .zero(z), .negative(n), .carry(c), .overflow(o));

  assign x3 = 1'b0;
  assign x4 = 1'b0;

  // Notes on the sheet:
  //   contents of rom_1 (hex, n*v repeats v):
  //   f,5
endmodule
