// Digital circuit MicroprogramExecution.dig as structural Verilog
module MicroprogramExecution (
  input  [1:0] sel,
  input  [7:0] Input,
  input  [3:0] sel_2,
  input  enPC,
  input  enOUT,
  input  enB,
  input  enA,
  input  [7:0] extDataBus,
  input  enMBR,
  input  clk,
  output [7:0] MemAddrBus,
  output [7:0] Disp,
  output [3:0] flags
);

  wire [7:0] A_q, alu_1_out, B_q, MBR_q, multiplexer_1_out;

  Register #(.Bits(8)) PC (.D(alu_1_out), .C(clk), .en(enPC), .Q(MemAddrBus));
  Register #(.Bits(8)) OUT (.D(alu_1_out), .C(clk), .en(enOUT), .Q(Disp));
  Register #(.Bits(8)) B (.D(alu_1_out), .C(clk), .en(enB), .Q(B_q));
  Register #(.Bits(8)) A (.D(alu_1_out), .C(clk), .en(enA), .Q(A_q));
  Register #(.Bits(8)) MBR (.D(extDataBus), .C(clk), .en(enMBR), .Q(MBR_q));
  ALU alu_1 (
    .A(A_q), .B(multiplexer_1_out), .F0(sel_2[0]), .F1(sel_2[1]), .F2(sel_2[2]), .F3(sel_2[3]),
    .out(alu_1_out), .zero(flags[0]), .negative(flags[1]), .carry(flags[2]), .overflow(flags[3]));
  Multiplexer #(.Bits(8), .Selector_Bits(2)) multiplexer_1 (
    .sel(sel), .in_0(Input), .in_1(MemAddrBus), .in_2(MBR_q), .in_3(B_q), .out(multiplexer_1_out));
endmodule
