// Digital circuit UserInput.dig as structural Verilog
module UserInput (
  input  clk,
  input  in_2,
  input  in_3,
  input  in_4,
  input  in_5,
  input  in_6,
  input  [7:0] extInp,
  input  [5:0] Instructions,
  output [5:0] PC,
  output [3:0] flags
);

  CPUControlUnit cpucontrolunit_1 (
    .clock(clk), .en1(in_6), .sel1(in_5), .Input(extInp), .en3(in_4), .en2(in_3), .A(Instructions),
    .sel2(in_2), .z(flags[0]), .n(flags[1]), .c(flags[2]), .o(flags[3]), .e(PC));
endmodule
