// Digital circuit demo-clock-th9ing.dig as structural Verilog
module demo_clock_th9ing (
  input  [3:0] in_2,
  input  in_3,
  input  in_4,
  output [3:0] out_1
);

  Register #(.Bits(4)) register_1 (.D(in_2), .C(in_3), .en(in_4), .Q(out_1));
endmodule
