// Digital circuit modifiedControlUnit.dig as structural Verilog
module modifiedControlUnit (
  input  clock,
  input  en1,
  input  sel1,
  input  [17:0] Input,
  input  en3,
  input  en2,
  input  [5:0] A,
  input  sel2,
  input  en4,
  input  en5,
  output z,
  output n,
  output c,
  output o,
  output [5:0] e
);

  wire cpudatapath_1_x3, cpudatapath_1_x4, not_1_out;
  wire [1:0] undriven;
  wire [3:0] cpudatapath_1_x1, cpudatapath_1_x2;
  wire [5:0] multiplexer_1_out;
  wire [17:0] control_store_d, MBR_q, MIR_q;

  Register #(.Bits(18)) MIR (.D(Input), .C(clock), .en(en4), .Q(MIR_q));
  Multiplexer #(.Bits(6)) multiplexer_1 (.in_0(A), .in_1(MIR_q[5:0]), .out(multiplexer_1_out));  // open: sel
  ROM #(.AddrBits(6), .Bits(18)) control_store (.A(multiplexer_1_out), .sel(sel1), .D(control_store_d));
  CPUDataPath cpudatapath_1 (
    .Out_Wr(MBR_q[0]), .PC_Wr(MBR_q[1]), .MBR_Wr(MBR_q[2]), .B_Wr(MBR_q[3]), .A_Wr(MBR_q[4]),
    .MUX_Ctrl(undriven), .z(z), .n(n), .c(c), .o(o), .x1(cpudatapath_1_x1), .x2(cpudatapath_1_x2),
    .x3(cpudatapath_1_x3), .x4(cpudatapath_1_x4));  // open: Input, ALU_Sel, clock, ROM_Sel
  not not_1 (not_1_out, clock);
  Register #(.Bits(18)) MBR (.D(control_store_d), .C(not_1_out), .en(en5), .Q(MBR_q));
  Seven_Seg_Hex seven_seg_hex_1 (.d(cpudatapath_1_x1), .dp(cpudatapath_1_x3));
  Register #(.Bits(6)) MPC ();  // open: D, C, en, Q
  Seven_Seg_Hex seven_seg_hex_2 (.d(cpudatapath_1_x2), .dp(cpudatapath_1_x4));
  // Pins of 6 and 18 bits meet at MIR_q
  // Pins of 8 and 18 bits meet at Input
  // Pins of 5 and 18 bits meet at MBR_q

  // Notes on the sheet:
  //   contents of control_store (hex, n*v repeats v):
  //   1004,21c0,31c8,800,0,60e0,70e1,0,9000,a010,0,c004,d0a0,e0a8,0
  //   ,10004,110a0,120a1,131c0,141c8,0,16100,17101,0,19000,1a002,0,1c200
  //   ,1d201,0,1f004,200a0,210a2,221c0,231c8,0,25400,26401,0,28480,29481
  //   ,0,2a000
endmodule
